# Fritzing sketch Embedded (saved by Fritzing 0.9.9b)
breadboards: 1

parts:
  L298N1 = L298N DC motor driver
  M1 = DC Motor
  M2 = DC Motor
  Part2 = Arduino Mega 2560 (Rev3)
  L298N2 = L298N DC motor driver
  M3 = DC Motor
  M4 = DC Motor
  DFRobot_DFPlayer_Mini1 = DFRobot DFPlayer Mini [part_number=DFR0299]
  SP1 = SPEAKER [package=pcb_mount_speaker]
  R1 = Photocell (LDR) [package=THT]
  LED1 = LED - 5mm [color="Red (633nm)" current=0.030 package="5 mm [THT]"]
  7_Segment1 = 7 Segment Display
  Part3 = Thumb Joystick
  M5 = fc-51 [package=THT]
  M6 = fc-51 [package=THT]
  Part4 = Arduino Uno (Rev3) - ICSP
  Part5 = Arduino Color LCD Shield
  LED2 = LED - 5mm [color="Red (633nm)" current=0.030 package="5 mm [THT]"]
  LED3 = LED - 5mm [color="Red (633nm)" current=0.030 package="5 mm [THT]"]

nets:
  N1: L298N1.OUT1, M2.pin_2
  N2: L298N1.OUT2, M2.pin_1
  N3: L298N1.OUT3, M1.pin_2
  N4: L298N1.OUT4, M1.pin_1
  12V: L298N1.12V, Part2.VIN, L298N2.12V
  GND: L298N1.GND, Part2.GND, L298N2.GND, DFRobot_DFPlayer_Mini1.GND-1, DFRobot_DFPlayer_Mini1.GND-2, R1.pin_0, LED1.anode, Part3.GND, M5.pin2, M6.pin2, Part4.GND, Part5.GND, LED2.anode, LED3.anode
  5V: L298N1.5V, Part2.5V, L298N2.5V, DFRobot_DFPlayer_Mini1.VCC, 7_Segment1.common_cathode, Part3.VCC, M5.pin3, M6.pin3
  N5: L298N1.ENA, Part2.D4_PWM
  N6: L298N1.ENB, Part2.D5_PWM
  N7: L298N1.IN1, Part2.D35
  N8: L298N1.IN2, Part2.D33
  N9: L298N1.IN3, Part2.D29
  N10: L298N1.IN4, Part2.D31
  N11: Part2.A10, M6.pin1
  N12: Part2.A0, M5.pin1
  N13: Part2.A1, R1.pin_1
  N14: Part2.A4, Part3.VERT
  N15: Part2.D21/SCL, Part4.A5/SCL, Part5.A5
  N16: Part2.D20/SDA, Part4.A4/SDA, Part5.A4
  N17: Part2.D10_PWM, DFRobot_DFPlayer_Mini1.RX
  N18: Part2.D9_PWM, DFRobot_DFPlayer_Mini1.TX
  N19: Part2.D8_PWM, LED1.cathode
  N20: Part2.D2_PWM, L298N2.ENA
  N21: Part2.D3_PWM, L298N2.ENB
  N22: Part2.D30, LED3.cathode
  N23: Part2.D32, LED2.cathode
  N24: Part2.D37, L298N2.IN3
  N25: Part2.D39, L298N2.IN4
  N26: Part2.D41, L298N2.IN2
  N27: Part2.D43, L298N2.IN1
  N28: Part2.D44, 7_Segment1.Segment_G
  N29: Part2.D46, 7_Segment1.Segment_F
  N30: Part2.D48, 7_Segment1.Segment_A
  N31: Part2.D49, 7_Segment1.Segment_C
  N32: Part2.D51, 7_Segment1.Segment_D
  N33: Part2.D52, 7_Segment1.Segment_B
  N34: Part2.D53, 7_Segment1.Segment_E
  N35: L298N2.OUT1, M4.pin_2
  N36: L298N2.OUT2, M4.pin_1
  N37: L298N2.OUT3, M3.pin_2
  N38: L298N2.OUT4, M3.pin_1
  N39: DFRobot_DFPlayer_Mini1.SPK_1, SP1.+
  N40: DFRobot_DFPlayer_Mini1.SPK_2, SP1.-
  N41: Part4.A0, Part5.A0
  N42: Part4.A1, Part5.A1
  N43: Part4.A2, Part5.A2
  N44: Part4.A3, Part5.A3
  N45: Part4.D8, Part5.D8
  N46: Part4.D9_PWM, Part5.D9
  N47: Part4.D10_PWM/SS, Part5.D10
  N48: Part4.D11_PWM/MOSI, Part5.D11
  N49: Part4.D12/MISO, Part5.D12
  N50: Part4.D13/SCK, Part5.D13
  N51: Part4.AREF, Part5.AREF
  N52: Part4.D0/RX, Part5.D0
  N53: Part4.D1/TX, Part5.D1
  N54: Part4.D2, Part5.D2
  N55: Part4.D3_PWM, Part5.D3
  N56: Part4.D4, Part5.D4
  N57: Part4.D5_PWM, Part5.D5
  N58: Part4.D6_PWM, Part5.D6
  N59: Part4.D7, Part5.D7
  N60: Part4.RESET, Part5.RESET
  3V3: Part4.3V3, Part5.3.3V
  5V_2: Part4.5V, Part5.5V
  VIN: Part4.VIN, Part5.VIN

notes:
  front Left Motor
  front Right Motor
  L298N Motor Driver Board
  back Right Motor
  back Left Motor

custom parts:
  L298N DC motor driver: 2x DC motor driver with 78M05 positive voltage regulator (7..35 V) L298N: max 46 V, 2 A Set 5 V Enable jumper to enable 5 V regultor (needed for the L298N) and +5 V output at screw terminal or supply external +5 V at screw terminal Set ENA and/or ENB to +5 V to enable motor permanently or supply ENA and/or ENB with PWM signal IN1 and IN2 set rotation directory for motor A (OUT1/OUT2) IN2 and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

// code stored in the sketch: Untitled4.ino
// Motor A FRONT WHEEL LEFT
int enA = 9;
int ForwardA = 8;
int BackwardA = 7;
// Motor B FRONT WHEEL RIGHT
int enB = 3;
int ForwardB = 5;
int BackwardB = 4;

// Motor C BACK WHEEL RIGHT
int enC = 6;
int ForwardC = 2;
int BackwardC = 12;

// Motor D BACK WHEEL LEFT
int enD = 10;
int ForwardD = 11;
int BackwardD = 13;

void setup() {
 
  pinMode(enA, OUTPUT);
  pinMode(enB, OUTPUT);
  pinMode(enC, OUTPUT);
  pinMode(enD, OUTPUT);
  pinMode(ForwardA, OUTPUT);
  pinMode(BackwardA, OUTPUT);
  pinMode(ForwardB, OUTPUT);
  pinMode(BackwardB, OUTPUT);
  pinMode(ForwardC, OUTPUT);
  pinMode(BackwardC, OUTPUT);
  pinMode(ForwardD, OUTPUT);
  pinMode(BackwardD, OUTPUT);
  //Motor A
  digitalWrite(enA, LOW);
  digitalWrite(ForwardA, HIGH);
  digitalWrite(BackwardA, LOW);
  
  // Motor B
  digitalWrite(enB, LOW);
  digitalWrite(ForwardB, HIGH);
  digitalWrite(BackwardB, LOW);
  
  // Motor C
  digitalWrite(enC, LOW);
  digitalWrite(ForwardC, HIGH);
  digitalWrite(BackwardC, LOW);

  // Motor D
    digitalWrite(enD, LOW);
  digitalWrite(ForwardD, HIGH);
  digitalWrite(BackwardD, LOW);
}
void forward(){
  digitalWrite(ForwardA, HIGH);
  digitalWrite(BackwardA, LOW);
  digitalWrite(ForwardB, HIGH);
  digitalWrite(BackwardB, LOW);
  digitalWrite(ForwardC, HIGH);
  digitalWrite(BackwardC, LOW);
  digitalWrite(ForwardD, HIGH);
  digitalWrite(BackwardD, LOW);
}

void forwardRight(){
  digitalWrite(ForwardA, HIGH);
  digitalWrite(BackwardA, LOW);
  digitalWrite(ForwardB, LOW);
  digitalWrite(BackwardB, HIGH);
  digitalWrite(ForwardC, HIGH);
  digitalWrite(BackwardC, LOW);
  digitalWrite(ForwardD, HIGH);
  digitalWrite(BackwardD, LOW);
}

void forwardleft(){
  digitalWrite(ForwardA, LOW);
  digitalWrite(BackwardA, HIGH);
  digitalWrite(ForwardB, HIGH);
  digitalWrite(BackwardB, LOW);
  digitalWrite(ForwardC, HIGH);
  digitalWrite(BackwardC, LOW);
  digitalWrite(ForwardD, HIGH);
  digitalWrite(BackwardD, LOW);
}

void backward(){
  digitalWrite(ForwardA, LOW);
  digitalWrite(BackwardA, HIGH);
  digitalWrite(ForwardB, LOW);
  digitalWrite(BackwardB, HIGH);
  digitalWrite(ForwardC, LOW);
  digitalWrite(BackwardC, HIGH);
  digitalWrite(ForwardD, LOW);
  digitalWrite(BackwardD, HIGH);
}

void backwardRight(){
  digitalWrite(ForwardA, LOW);
  digitalWrite(BackwardA, HIGH);
  digitalWrite(ForwardB, HIGH);
  digitalWrite(BackwardB, LOW);
  digitalWrite(ForwardC, LOW);
  digitalWrite(BackwardC, HIGH);
  digitalWrite(ForwardD, LOW);
  digitalWrite(BackwardD, HIGH);
}

void backwardLeft(){
  digitalWrite(ForwardA, HIGH);
  digitalWrite(BackwardA, LOW);
  digitalWrite(ForwardB, LOW);
  digitalWrite(BackwardB, HIGH);
  digitalWrite(ForwardC, LOW);
  digitalWrite(BackwardC, HIGH);
  digitalWrite(ForwardD, LOW);
  digitalWrite(BackwardD, HIGH);
}


void loop() {
	forward();
}
